// Logisim project MIPS.circ as structural Verilog: 8 circuits, main circuit Control_Unit
module Control_Unit (
  input  [3:0] Opcode,
  output RegDst,
  output Jump,
  output Branch,
  output MemRead,
  output MemtoReg,
  output [2:0] ALUOp,
  output MemWrite,
  output ALUSrc,
  output RegWrite,
  output Shift
);

  ROM #(.addrWidth(4), .dataWidth(12)) rom_1 (
    .addr(Opcode), .data({RegDst, Jump, Branch, MemRead, MemtoReg, ALUOp, MemWrite, ALUSrc, RegWrite, Shift}));  // open: sel

  // Notes on the sheet:
  //   contents of rom_1 (hex, n*v repeats v):
  //   a10 986 53 42 836 12 400 a10 816 22 63 826 806 32 2 80c
endmodule

module test (
  input  [3:0] in_1,
  input  [7:0] in_2,
  input  [7:0] in_3,
  input  [3:0] in_4,
  input  [3:0] in_5,
  input  [2:0] in_6,
  input  [3:0] in_7,
  input  [7:0] in_8,
  input  in_9,
  input  in_10,
  input  [7:0] in_11,
  input  [7:0] in_12,
  input  in_13,
  output [2:0] out_14,
  output [7:0] out_15,
  output [7:0] out_16,
  output [7:0] out_17,
  output [7:0] out_18
);

  wire alu_8_by_art_1_p5, alu_8_by_art_1_p7, clock_1_out, clock_2_out, control_unit_1_alusrc,
       control_unit_1_branch, control_unit_1_jump, control_unit_1_memread, control_unit_1_memtoreg,
       control_unit_1_memwrite, control_unit_1_regdst, control_unit_1_regwrite, control_unit_1_shift;

  Clock clock_1 (.out(clock_1_out));
  Control_Unit control_unit_1 (
    .Opcode(in_1), .RegDst(control_unit_1_regdst), .Jump(control_unit_1_jump),
    .Branch(control_unit_1_branch), .MemRead(control_unit_1_memread), .MemtoReg(control_unit_1_memtoreg),
    .ALUOp(out_14), .MemWrite(control_unit_1_memwrite), .ALUSrc(control_unit_1_alusrc),
    .RegWrite(control_unit_1_regwrite), .Shift(control_unit_1_shift));
  Register_File register_file_1 (
    .Read_Reg_1(in_4), .Read_Reg_2(in_5), .Write_Reg(in_7), .Write_Data(in_8), .Clock(clock_1_out),
    .Reg_Write(in_10), .Read_Data_1(out_16), .Read_Data_2(out_17));  // open: zero, t0, t1, t2, t3, t4, sp, Reset
  Clock clock_2 (.out(clock_2_out));
  Program_Counter program_counter_1 ();  // open: PC_input, Clock, Reset, PC_output
  Data_Memory data_memory_1 (
    .Address(in_11), .Write_Data(in_12), .Clock(clock_2_out), .Read_Data(out_18));  // open: MemRead, MemWrite
  // ALU_8_by_ART alu_8_by_art_1: pin names not known; wires that end beside it: in_9, in_2, in_3, in_6, alu_8_by_art_1_p5, out_15, alu_8_by_art_1_p7, alu_8_by_art_1_p5, alu_8_by_art_1_p7
endmodule

module Register_File (
  input  [3:0] Read_Reg_1,
  input  [3:0] Read_Reg_2,
  input  Reset,
  input  [3:0] Write_Reg,
  input  [7:0] Write_Data,
  input  Clock,
  input  Reg_Write,
  output [7:0] Read_Data_1,
  output [7:0] Read_Data_2,
  output [7:0] zero,
  output [7:0] t0,
  output [7:0] t1,
  output [7:0] t2,
  output [7:0] t3,
  output [7:0] t4,
  output [7:0] sp
);

  wire and_1_out, decoder_1_out0, decoder_1_out1, decoder_1_out2, decoder_1_out3, decoder_1_out4,
       decoder_1_out5, decoder_1_out6, multiplexer_3_out, multiplexer_4_out, multiplexer_5_out,
       multiplexer_6_out, multiplexer_7_out, multiplexer_8_out;
  wire [2:0] multiplexer_2_out;
  wire [7:0] multiplexer_1_out;

  Multiplexer #(.width(8), .enable("false")) multiplexer_1 (
    .in0(Write_Data), .in1({8{1'b0}}), .out(multiplexer_1_out), .sel(Reset));
  and and_1 (and_1_out, Clock, Reg_Write);
  Decoder #(.select(3), .enable("false")) decoder_1 (
    .out0(decoder_1_out0), .out1(decoder_1_out1), .out2(decoder_1_out2), .out3(decoder_1_out3),
    .out4(decoder_1_out4), .out5(decoder_1_out5), .out6(decoder_1_out6), .sel(multiplexer_2_out));  // open: out7
  Multiplexer #(.width(3), .enable("false")) multiplexer_2 (
    .in0(3'b000), .in1(Write_Reg[2:0]), .out(multiplexer_2_out), .sel(and_1_out));
  Register u_zero (.D({8{1'b0}}), .en(1'b1), .Q(zero), .clk(decoder_1_out0));  // open: clr
  Register u_t0 (.D(multiplexer_1_out), .en(1'b1), .Q(t0), .clk(multiplexer_3_out));  // open: clr
  Multiplexer #(.enable("false")) multiplexer_3 (
    .in0(decoder_1_out1), .in1(1'b1), .out(multiplexer_3_out), .sel(Reset));
  Register u_t1 (.D(multiplexer_1_out), .en(1'b1), .Q(t1), .clk(multiplexer_4_out));  // open: clr
  Multiplexer #(.enable("false")) multiplexer_4 (
    .in0(decoder_1_out2), .in1(1'b1), .out(multiplexer_4_out), .sel(Reset));
  Register u_t2 (.D(multiplexer_1_out), .en(1'b1), .Q(t2), .clk(multiplexer_5_out));  // open: clr
  Multiplexer #(.enable("false")) multiplexer_5 (
    .in0(decoder_1_out3), .in1(1'b1), .out(multiplexer_5_out), .sel(Reset));
  Multiplexer #(.enable("false")) multiplexer_6 (
    .in0(decoder_1_out4), .in1(1'b1), .out(multiplexer_6_out), .sel(Reset));
  Register u_t3 (.D(multiplexer_1_out), .en(1'b1), .Q(t3), .clk(multiplexer_6_out));  // open: clr
  Register u_t4 (.D(multiplexer_1_out), .en(1'b1), .Q(t4), .clk(multiplexer_7_out));  // open: clr
  Multiplexer #(.enable("false")) multiplexer_7 (
    .in0(decoder_1_out5), .in1(1'b1), .out(multiplexer_7_out), .sel(Reset));
  Register u_sp (.D(multiplexer_1_out), .en(1'b1), .Q(sp), .clk(multiplexer_8_out));  // open: clr
  Multiplexer #(.enable("false")) multiplexer_8 (
    .in0(decoder_1_out6), .in1(1'b1), .out(multiplexer_8_out), .sel(Reset));
  Multiplexer #(.select(3), .width(8), .enable("false")) multiplexer_9 (
    .in0(zero), .in1(t0), .in2(t1), .in3(t2), .in4(t3), .in5(t4), .in6(sp), .out(Read_Data_1),
    .sel(Read_Reg_1[2:0]));  // open: in7
  Multiplexer #(.select(3), .width(8), .enable("false")) multiplexer_10 (
    .in0(zero), .in1(t0), .in2(t1), .in3(t2), .in4(t3), .in5(t4), .in6(sp), .out(Read_Data_2),
    .sel(Read_Reg_2[2:0]));  // open: in7
endmodule

module Program_Counter (
  input  [7:0] PC_input,
  input  Clock,
  input  Reset,
  output [7:0] PC_output
);

  Register #(.trigger("falling")) register_1 (.D(PC_input), .en(1'b1), .Q(PC_output), .clk(Clock), .clr(Reset));
endmodule

module Instruction_Memory (
  input  [7:0] PC,
  output [7:0] Jump,
  output [3:0] opcode,
  output [3:0] rs,
  output [3:0] rt,
  output [3:0] rd,
  output [3:0] shamt,
  output [7:0] Address_Immediate
);

  ROM #(.dataWidth(20)) rom_1 (.addr(PC), .data({opcode, Jump, Address_Immediate}));  // open: sel

  assign rd = Address_Immediate[7:4];
  assign rs = Jump[7:4];
  assign rt = Jump[3:0];
  assign shamt = Address_Immediate[3:0];

  // Notes on the sheet:
  //   contents of rom_1 (hex, n*v repeats v):
  //   c06ff c110a c220f e1230 52140 c0514 85605 d1230 42403 91650 b5601 20632 a0541 34310 f6100 16500
  //   60100
endmodule

module Data_Memory (
  input  MemRead,
  input  MemWrite,
  input  [7:0] Address,
  input  [7:0] Write_Data,
  input  Clock,
  output [7:0] Read_Data
);

  RAM #(.bus("separate")) ram_1 (
    .addr(Address), .din(Write_Data), .data(Read_Data), .str(MemWrite), .clk(Clock), .ld(MemRead));  // open: sel, clr
endmodule

module main (
  input  Reset,
  input  Clock,
  output [7:0] PC,
  output [7:0] zero,
  output [7:0] to,
  output [7:0] t1,
  output [7:0] t2,
  output [7:0] t3,
  output [7:0] t4,
  output [7:0] sp
);

  wire alu_8_by_art_1_p4, and_1_out, and_2_out, control_unit_1_alusrc, control_unit_1_branch,
       control_unit_1_jump, control_unit_1_memread, control_unit_1_memtoreg, control_unit_1_memwrite,
       control_unit_1_regdst, control_unit_1_regwrite, control_unit_1_shift, multiplexer_6_out, nor_1_out,
       not_1_out;
  wire [2:0] control_unit_1_aluop;
  wire [3:0] instruction_memory_1_opcode, instruction_memory_1_rd, instruction_memory_1_rs,
       instruction_memory_1_rt, instruction_memory_1_shamt, multiplexer_2_out;
  wire [7:0] adder_1_out, adder_2_out, alu_8_by_art_1_p5, bit_extender_1_out, data_memory_1_read_data,
       instruction_memory_1_address_immediate, instruction_memory_1_jump, multiplexer_1_out,
       multiplexer_3_out, multiplexer_4_out, multiplexer_5_out, multiplexer_7_out,
       register_file_1_read_data_1, register_file_1_read_data_2;

  Program_Counter program_counter_1 (.PC_input(multiplexer_1_out), .Clock(Clock), .Reset(Reset), .PC_output(PC));
  Multiplexer #(.width(8), .enable("false")) multiplexer_1 (
    .in0(multiplexer_5_out), .in1(instruction_memory_1_jump), .out(multiplexer_1_out),
    .sel(control_unit_1_jump));
  Adder adder_1 (.a(PC), .b(8'h1), .out(adder_1_out));  // open: cin, cout
  Instruction_Memory instruction_memory_1 (
    .PC(PC), .Jump(instruction_memory_1_jump), .opcode(instruction_memory_1_opcode),
    .rs(instruction_memory_1_rs), .rt(instruction_memory_1_rt), .rd(instruction_memory_1_rd),
    .shamt(instruction_memory_1_shamt), .Address_Immediate(instruction_memory_1_address_immediate));
  Multiplexer #(.width(4), .enable("false")) multiplexer_2 (
    .in0(instruction_memory_1_rd), .in1(instruction_memory_1_rt), .out(multiplexer_2_out),
    .sel(control_unit_1_regdst));
  assign bit_extender_1_out = {{4{1'b0}}, instruction_memory_1_shamt};  // Bit_Extender bit_extender_1
  Control_Unit control_unit_1 (
    .Opcode(instruction_memory_1_opcode), .RegDst(control_unit_1_regdst), .Jump(control_unit_1_jump),
    .Branch(control_unit_1_branch), .MemRead(control_unit_1_memread), .MemtoReg(control_unit_1_memtoreg),
    .ALUOp(control_unit_1_aluop), .MemWrite(control_unit_1_memwrite), .ALUSrc(control_unit_1_alusrc),
    .RegWrite(control_unit_1_regwrite), .Shift(control_unit_1_shift));
  Register_File register_file_1 (
    .Read_Reg_1(instruction_memory_1_rs), .Read_Reg_2(instruction_memory_1_rt),
    .Write_Reg(multiplexer_2_out), .Write_Data(multiplexer_7_out), .Clock(Clock),
    .Reg_Write(control_unit_1_regwrite), .Read_Data_1(register_file_1_read_data_1),
    .Read_Data_2(register_file_1_read_data_2), .zero(zero), .t0(to), .t1(t1), .t2(t2), .t3(t3), .t4(t4),
    .sp(sp), .Reset(Reset));
  nor nor_1 (nor_1_out, instruction_memory_1_opcode[0], instruction_memory_1_opcode[1], instruction_memory_1_opcode[2], instruction_memory_1_opcode[3]);
  Adder adder_2 (.a(adder_1_out), .b(instruction_memory_1_address_immediate), .out(adder_2_out));  // open: cin, cout
  Multiplexer #(.width(8), .enable("false")) multiplexer_3 (
    .in0(register_file_1_read_data_1), .in1(bit_extender_1_out), .out(multiplexer_3_out),
    .sel(control_unit_1_shift));
  Multiplexer #(.width(8), .enable("false")) multiplexer_4 (
    .in0(register_file_1_read_data_2), .in1(instruction_memory_1_address_immediate), .out(multiplexer_4_out),
    .sel(control_unit_1_alusrc));
  // ALU_8_by_ART alu_8_by_art_1: pin names not known; wires that end beside it: multiplexer_3_out, multiplexer_4_out, control_unit_1_aluop, alu_8_by_art_1_p4, alu_8_by_art_1_p5
  Multiplexer #(.width(8), .enable("false")) multiplexer_5 (
    .in0(adder_1_out), .in1(adder_2_out), .out(multiplexer_5_out), .sel(multiplexer_6_out));
  and and_1 (and_1_out, control_unit_1_branch, alu_8_by_art_1_p4);
  not not_1 (not_1_out, alu_8_by_art_1_p4);
  Multiplexer #(.enable("false")) multiplexer_6 (
    .in0(and_1_out), .in1(and_2_out), .out(multiplexer_6_out), .sel(nor_1_out));
  Multiplexer #(.width(8), .enable("false")) multiplexer_7 (
    .in0(alu_8_by_art_1_p5), .in1(data_memory_1_read_data), .out(multiplexer_7_out),
    .sel(control_unit_1_memtoreg));
  Data_Memory data_memory_1 (
    .MemRead(control_unit_1_memread), .MemWrite(control_unit_1_memwrite), .Address(alu_8_by_art_1_p5),
    .Write_Data(register_file_1_read_data_2), .Clock(Clock), .Read_Data(data_memory_1_read_data));
  and and_2 (and_2_out, nor_1_out, not_1_out);
endmodule

module mips_block (
  input  Reset,
  output [7:0] PC,
  output [7:0] zero,
  output [7:0] t0,
  output [7:0] t1,
  output [7:0] t2,
  output [7:0] t3,
  output [7:0] t4,
  output [7:0] sp
);

  wire Clock_out;

  Clock Clock (.out(Clock_out));
  main main_1 (
    .Reset(Reset), .PC(PC), .to(t0), .t1(t1), .t2(t2), .t3(t3), .t4(t4), .sp(sp), .Clock(Clock_out),
    .zero(zero));
endmodule
